// Logisim project fifth-lorteau-brodu.circ as structural Verilog: 19 circuits, main circuit FIFTH
// Reset
module FIFTH (
  input  Reset
);

  wire CBOUT, CLK, Halt, isPopAdr, isPushAdr, resetSig;
  wire [1:0] SPselC, SPselD, WselC, WselD;
  wire [2:0] FLAGS, WhereToWrite;
  wire [3:0] _4_op;
  wire [4:0] _5_op;
  wire [5:0] _6_op, OPCODE;
  wire [9:0] rom_1_data;
  wire [15:0] C_STACK_SP, C_STACK_SP_1,
       calcule_la_vouvelle_valeur_du_registre_PC_apres_chauqe_instruction_new_pc, D_STACK_SP, D_STACK_SP_1,
       PC, TestResult, ToWrite, UAL_RESULT, valInstr, ValRam;

  Controlleur \calcule_les_signaux_nécéssaire_à_chaque_sous_circuits  (
    .OPCODE(OPCODE), .resetSig(Reset), ._6_OP(_6_op), ._5_OP(_5_op), ._4_OP(_4_op), .ResetSig_2(resetSig),
    .SpselD(SPselD), .WselD(WselD), .SPselC(SPselC), .WselC(WselC), .Halt(Halt), .WhereToWrite(WhereToWrite),
    .isPushAdr(isPushAdr), .isPopAdr(isPopAdr));
  U_A_L UAL (.A(D_STACK_SP_1), .B(D_STACK_SP), .s(UAL_RESULT), .Cbout(CBOUT), .FLAGS(FLAGS), .OPCODE(_4_op));
  Tester Tester (.OF_SF_ZF(FLAGS), .OPCODE(_6_op), .Output(TestResult));
  RAM #(.addrWidth(16), .dataWidth(16), .bus("separate")) ram_1 (
    .addr(valInstr), .din(D_STACK_SP), .data(ValRam), .str(isPopAdr), .clk(CLK), .ld(isPushAdr),
    .clr(resetSig));  // open: sel
  Update_PC calcule_la_vouvelle_valeur_du_registre_PC_apres_chauqe_instruction (
    .opcode(_6_op), .Stack_SP(C_STACK_SP), .instr_parameter(valInstr), .PreviousPC(PC),
    .New_PC(calcule_la_vouvelle_valeur_du_registre_PC_apres_chauqe_instruction_new_pc),
    .ResultatTest(D_STACK_SP));
  Pile_Appel Call_Stack (
    .CLK(CLK), .ResetSig(resetSig), .Stack_SP_1(C_STACK_SP_1), .Stack_SP(C_STACK_SP), .Halt(Halt),
    .PselC(SPselC), .WselC(WselC), .opcode(_5_op), .PC(PC));
  ROM #(.addrWidth(16), .dataWidth(16)) rom_1 (.addr(PC), .data({OPCODE, rom_1_data}));  // open: sel
  assign valInstr = {{6{1'b0}}, rom_1_data};  // Bit_Extender bit_extender_1
  Register #(.width(16)) u_PC (
    .D(calcule_la_vouvelle_valeur_du_registre_PC_apres_chauqe_instruction_new_pc), .en(Halt), .Q(PC),
    .clk(CLK), .clr(resetSig));
  Clock clock_1 (.out(CLK));
  \Pile_Donnée  Data_Stack (
    .opcode(_5_op), .CLK(CLK), .ResetSig(resetSig), .Stack_SP_1(D_STACK_SP_1), .Stack_SP(D_STACK_SP),
    .IMPUT(ToWrite), .SPselD(SPselD), .WselD(WselD), .Halt(Halt));
  Multiplexer #(.select(3), .width(16), .enable("false")) multiplexer_1 (
    .in0(UAL_RESULT), .in1(TestResult), .in2(D_STACK_SP), .in3(valInstr), .in4(ValRam), .out(ToWrite),
    .sel(WhereToWrite));  // open: in5, in6, in7

  // Notes on the sheet:
  //   Reset remet à zero tous les registres du processeur et de la RAM
  //   retourne le résustat du test lors d'une instruction GT LT EQ
  //   realise les opérations demandées entre les deux valeurs du haut de la pile
  //   mais elle ne sert ici que lors d'une ecriture
  //   la ram permet le stockage et la lecture de valeurs en dehors des registres
  //   valinstr change beaucoup car elle est tout le temps interprété comme une adresse
  //   la rom contient le programme (opcode et parametres d'instructions)
  //   la pile d'appel, à chaque tic d'horloge on lit les deux valeurs du haut de la pile
  //   et on y éventuellement une adresse de retour (PC+1)
  //   contents of rom_1 (hex, n*v repeats v):
  //   4405 5404 5000 6000 5c00 4400 3000 400b 4c00 4401 3810 5c00 4401 400 5404 c00 5800
  //   en etant le parametre sur 16 bits
  //   horloge (à faire tourner à la main)
  //   la pile de données on y empile les résultats des différentes instructions
  //   en fonction de l'instruction la valeur écrite dans stack SP peut provenir
  //   de différents endroits du processeur
  //   On selectionne la bonne valeur à ecrire en fonction de l'instruction courante
  //   on utilise le signale WhereToWrite qui est implémenté dans le controlleur
endmodule

module U_A_L (
  input  [3:0] OPCODE,
  input  [15:0] A,
  input  [15:0] B,
  output [15:0] s,
  output Cbout,
  output [2:0] FLAGS
);

  wire Borrow, Carry;
  wire [3:0] bitselector_1_out, bitselector_2_out, OP_t;
  wire [15:0] ADD, AND, DIV, DIV_t, MUL, NEG, NOT, OR, OR_t, REM, RESULT_t, SHL, SRA, SUB;

  Adder #(.width(16)) adder_1 (.a(A), .b(B), .out(ADD), .cout(Carry));  // open: cin
  Subtractor #(.width(16)) subtractor_1 (.a(A), .b(B), .out(SUB), .bout(Borrow));  // open: bin
  Divider #(.width(16)) divider_1 (.a(A), .b(B), .out(DIV));  // open: upper, rem
  Divider #(.width(16)) divider_2 (.a(A), .b(B), .rem(REM));  // open: out, upper
  Multiplier #(.width(16)) multiplier_1 (.a(A), .b(B), .out(MUL));  // open: cin, cout
  assign AND = A & B;  // AND_Gate and_1, 16 bits wide
  assign OR = A | B;  // OR_Gate or_1, 16 bits wide
  BitSelector #(.width(16), .group(4)) bitselector_1 (.in(B), .out(bitselector_1_out), .sel(2'b00));
  BitSelector #(.width(16), .group(4)) bitselector_2 (.in(B), .out(bitselector_2_out), .sel(2'b00));
  Negator #(.width(16)) negator_1 (.in(A), .out(NEG));
  assign NOT = ~A;  // NOT_Gate not_1, 16 bits wide
  Shifter #(.width(16)) shifter_1 (.in(A), .\dist (bitselector_1_out), .out(SHL));
  Shifter #(.width(16), .shift("ar")) shifter_2 (.in(A), .\dist (bitselector_2_out), .out(SRA));
  Multiplexer #(.select(4), .enable("false")) multiplexer_1 (
    .in0(Carry), .in1(Borrow), .in11(Borrow), .in12(Borrow), .in13(Borrow), .out(Cbout), .sel(OPCODE));  // open: in2, in3, in4, in5, in6, in7, in8, in9, in10, in14, in15
  Multiplexer #(.select(4), .width(16), .enable("false")) multiplexer_2 (
    .in0(ADD), .in1(SUB), .in2(NEG), .in3(MUL), .in4(DIV_t), .in5(REM), .in6(NOT), .in7(AND), .in8(OR_t),
    .in9(SHL), .in10(SRA), .in11(SUB), .in12(SUB), .in13(SUB), .out(s), .sel(OPCODE));  // open: in14, in15
  Flags u_FLAGS (.RESULT(RESULT_t), .A(A), .B(B), .OPCODE(OP_t), .Flags(FLAGS));

  // Other names for the same wires on the sheet: OP[3:0] = OPCODE; RESULT[15:0] = s

  // Notes on the sheet:
  //   Deux entrée A et B. 
  //   On effectue toute les opérations demandées en parallèle 
  //   puis on envois la bonne sortie dans le résultat a l’aide d’un multiplexeur.
  //   On envoit également A B et le résultat dans le circuit qui calcule les drapeaux
endmodule

module Tester (
  input  [2:0] OF_SF_ZF,
  input  [5:0] OPCODE,
  output [15:0] Output
);

  wire and_1_out, and_2_out, and_3_out, EQ_out, GT_out, LT_out, or_1_out, or_2_out;

  and LT (LT_out, ~OPCODE[5], ~OPCODE[4], OPCODE[3], ~OPCODE[2], OPCODE[1], OPCODE[0]);  // AND_Gate
  and EQ (EQ_out, ~OPCODE[5], ~OPCODE[4], OPCODE[3], OPCODE[2], ~OPCODE[1], ~OPCODE[0]);  // AND_Gate
  and GT (GT_out, ~OPCODE[5], ~OPCODE[4], OPCODE[3], OPCODE[2], ~OPCODE[1], OPCODE[0]);  // AND_Gate
  or or_1 (or_1_out, OF_SF_ZF[1], OF_SF_ZF[2]);
  and and_1 (and_1_out, OF_SF_ZF[0], ~OF_SF_ZF[1], ~OF_SF_ZF[2], EQ_out);  // AND_Gate
  and and_2 (and_2_out, ~OF_SF_ZF[0], ~OF_SF_ZF[1], ~OF_SF_ZF[2], GT_out);  // AND_Gate
  and and_3 (and_3_out, ~OF_SF_ZF[0], or_1_out, LT_out);  // AND_Gate
  assign Output = {{15{1'b0}}, or_2_out};  // Bit_Extender bit_extender_1
  or or_2 (or_2_out, and_3_out, and_1_out, and_2_out);

  // Notes on the sheet:
  //   Le testeur vérifie d’abord quelle instruction de test à été  demandée
  //    puis calcule le résultat du test à l’aide des drapeaux
endmodule

module \Pile_Donnée  (
  input  [1:0] SPselD,
  input  [4:0] opcode,
  input  Halt,
  input  CLK,
  input  ResetSig,
  input  [15:0] IMPUT,
  input  [1:0] WselD,
  output [15:0] Stack_SP_1,
  output [15:0] Stack_SP
);

  wire [3:0] multiplexer_1_out, multiplexer_2_out, SP, SP_1, SP_1_t;
  wire [15:0] R0, R1, R2, R3, R4, R5, R6, R7, R8, R9, R10, R11, R12, R13, R14, R15, WR0, WR1, WR2, WR3, WR4,
       WR5, WR6, WR7, WR8, WR9, WR10, WR11, WR12, WR13, WR14, WR15;

  Adder #(.width(4)) adder_1 (.a(SP), .b(4'b0001), .out(SP_1));  // open: cin, cout
  Subtractor #(.width(4)) subtractor_1 (.a(SP), .b(4'b0001), .out(SP_1_t));  // open: bin, bout
  Multiplexer #(.select(2), .width(4), .enable("false")) multiplexer_1 (
    .in0(4'b0000), .in1(SP_1), .in2(SP), .in3(SP_1_t), .out(multiplexer_1_out), .sel(SPselD));
  Register #(.width(4)) u_SP (.D(multiplexer_1_out), .en(Halt), .Q(SP), .clk(CLK), .clr(ResetSig));
  Register #(.width(16)) u_R8 (.D(WR8), .en(Halt), .Q(R8), .clk(CLK), .clr(ResetSig));
  Register #(.width(16)) u_R0 (.D(WR0), .en(Halt), .Q(R0), .clk(CLK), .clr(ResetSig));
  Multiplexer #(.select(2), .width(4), .enable("false")) multiplexer_2 (
    .in0(SP), .in1(SP_1_t), .in2(SP_1), .in3(4'b0000), .out(multiplexer_2_out), .sel(WselD));
  Register #(.width(16)) u_R9 (.D(WR9), .en(Halt), .Q(R9), .clk(CLK), .clr(ResetSig));
  Register #(.width(16)) u_R1 (.D(WR1), .en(Halt), .Q(R1), .clk(CLK), .clr(ResetSig));
  Register #(.width(16)) u_R10 (.D(WR10), .en(Halt), .Q(R10), .clk(CLK), .clr(ResetSig));
  Register #(.width(16)) u_R2 (.D(WR2), .en(Halt), .Q(R2), .clk(CLK), .clr(ResetSig));
  Multiplexer #(.select(4), .width(16), .enable("false")) multiplexer_3 (
    .in0(R0), .in1(R1), .in2(R2), .in3(R3), .in4(R4), .in5(R5), .in6(R6), .in7(R7), .in8(R8), .in9(R9),
    .in10(R10), .in11(R11), .in12(R12), .in13(R13), .in14(R14), .in15(R15), .out(Stack_SP_1), .sel(SP_1));
  Multiplexer #(.select(4), .width(16), .enable("false")) multiplexer_4 (
    .in0(R0), .in1(R1), .in2(R2), .in3(R3), .in4(R4), .in5(R5), .in6(R6), .in7(R7), .in8(R8), .in9(R9),
    .in10(R10), .in11(R11), .in12(R12), .in13(R13), .in14(R14), .in15(R15), .out(Stack_SP), .sel(SP));
  Demultiplexer #(.select(4), .width(16), .tristate("true"), .enable("false")) demultiplexer_1 (
    .out0(WR0), .out1(WR1), .out2(WR2), .out3(WR3), .out4(WR4), .out5(WR5), .out6(WR6), .out7(WR7),
    .out8(WR8), .out9(WR9), .out10(WR10), .out11(WR11), .out12(WR12), .out13(WR13), .out14(WR14),
    .out15(WR15), .in(IMPUT), .sel(multiplexer_2_out));
  Register #(.width(16)) u_R11 (.D(WR11), .en(Halt), .Q(R11), .clk(CLK), .clr(ResetSig));
  Register #(.width(16)) u_R3 (.D(WR3), .en(Halt), .Q(R3), .clk(CLK), .clr(ResetSig));
  Register #(.width(16)) u_R12 (.D(WR12), .en(Halt), .Q(R12), .clk(CLK), .clr(ResetSig));
  Register #(.width(16)) u_R4 (.D(WR4), .en(Halt), .Q(R4), .clk(CLK), .clr(ResetSig));
  Register #(.width(16)) u_R13 (.D(WR13), .en(Halt), .Q(R13), .clk(CLK), .clr(ResetSig));
  Register #(.width(16)) u_R5 (.en(Halt), .Q(R5), .clk(CLK), .clr(ResetSig));  // open: D
  Register #(.width(16)) u_R14 (.D(WR14), .en(Halt), .Q(R14), .clk(CLK), .clr(ResetSig));
  Register #(.width(16)) u_R6 (.D(WR6), .en(Halt), .Q(R6), .clk(CLK), .clr(ResetSig));
  Register #(.width(16)) u_R15 (.D(WR15), .en(Halt), .Q(R15), .clk(CLK), .clr(ResetSig));
  Register #(.width(16)) u_R7 (.D(WR7), .en(Halt), .Q(R7), .clk(CLK), .clr(ResetSig));

  // Other names for the same wires on the sheet: OP[4:0] = opcode

  // Notes on the sheet:
  //   si Halt vaut 0 les registres ne répondent plus aux tics d'horloge
  //   Circuit pour lire dans le registre pointé par SP
  //   Le multiplexeur oriente vers la sortie  du registre pointé (lecture)
  //   Le multiplexeur oriente vers la sortie  du registre pointé (lecture)
  //   resteSig remet tous les registres à 0 si à l'état 1
  //   Circuit pour lire dans le registre pointé par SP+1
  //   la pile est constitué de nombreux registres connectés à la meme horloge
  //   incrémente, décrémente, passe à 0 ou laisse à 0 la valeur  du registre SP à chaque instruction en fonction de SPsel
  //   R est la sortie des registres pour lire les données 
  //   WR est l'entrée des registre pour ecrire les données
  //   Circuit pour écrire dans un registre
  //   Même principe, seulement on accès à l’entrée du registre (écriture)
  //   On utilise un multiplexeur annexe car on doit pouvoir
  //   écrire dans SP, SP+1 ou SP-1. Cette information est donnée par Wsel
endmodule

module Pile_Appel (
  input  [4:0] opcode,
  input  Halt,
  input  [1:0] PselC,
  input  CLK,
  input  [15:0] PC,
  input  ResetSig,
  input  [1:0] WselC,
  output [15:0] Stack_SP_1,
  output [15:0] Stack_SP
);

  wire [3:0] multiplexer_1_out, multiplexer_2_out, SP, SP_1, SP_1_t;
  wire [15:0] PC_1, R0, R1, R2, R3, R4, R5, R6, R7, R8, R9, R10, R11, R12, R13, R14, R15, WR0, WR1, WR2, WR3,
       WR4, WR5, WR6, WR7, WR8, WR9, WR10, WR11, WR12, WR13, WR14, WR15;

  Adder #(.width(4)) adder_1 (.a(SP), .b(4'b0001), .out(SP_1));  // open: cin, cout
  Subtractor #(.width(4)) subtractor_1 (.a(SP), .b(4'b0001), .out(SP_1_t));  // open: bin, bout
  Multiplexer #(.select(2), .width(4), .enable("false")) multiplexer_1 (
    .in0(4'b0000), .in1(SP_1), .in2(SP), .in3(SP_1_t), .out(multiplexer_1_out), .sel(PselC));
  Register #(.width(16)) u_R8 (.D(WR8), .en(Halt), .Q(R8), .clk(CLK), .clr(ResetSig));
  Register #(.width(16)) u_R0 (.D(WR0), .en(Halt), .Q(R0), .clk(CLK), .clr(ResetSig));
  Register #(.width(4)) u_SP (.D(multiplexer_1_out), .en(Halt), .Q(SP), .clk(CLK), .clr(ResetSig));
  Multiplexer #(.select(2), .width(4), .enable("false")) multiplexer_2 (
    .in0(SP), .in1(SP_1_t), .in2(SP_1), .in3(4'b0000), .out(multiplexer_2_out), .sel(WselC));
  Register #(.width(16)) u_R9 (.D(WR9), .en(Halt), .Q(R9), .clk(CLK), .clr(ResetSig));
  Register #(.width(16)) u_R1 (.D(WR1), .en(Halt), .Q(R1), .clk(CLK), .clr(ResetSig));
  Register #(.width(16)) u_R10 (.D(WR10), .en(Halt), .Q(R10), .clk(CLK), .clr(ResetSig));
  Register #(.width(16)) u_R2 (.D(WR2), .en(Halt), .Q(R2), .clk(CLK), .clr(ResetSig));
  Multiplexer #(.select(4), .width(16), .enable("false")) multiplexer_3 (
    .in0(R0), .in1(R1), .in2(R2), .in3(R3), .in4(R4), .in5(R5), .in6(R6), .in7(R7), .in8(R8), .in9(R9),
    .in10(R10), .in11(R11), .in12(R12), .in13(R13), .in14(R14), .in15(R15), .out(Stack_SP_1), .sel(SP_1));
  Multiplexer #(.select(4), .width(16), .enable("false")) multiplexer_4 (
    .in0(R0), .in1(R1), .in2(R2), .in3(R3), .in4(R4), .in5(R5), .in6(R6), .in7(R7), .in8(R8), .in9(R9),
    .in10(R10), .in11(R11), .in12(R12), .in13(R13), .in14(R14), .in15(R15), .out(Stack_SP), .sel(SP));
  Demultiplexer #(.select(4), .width(16), .tristate("true"), .enable("false")) demultiplexer_1 (
    .out0(WR0), .out1(WR1), .out2(WR2), .out3(WR3), .out4(WR4), .out5(WR5), .out6(WR6), .out7(WR7),
    .out8(WR8), .out9(WR9), .out10(WR10), .out11(WR11), .out12(WR12), .out13(WR13), .out14(WR14),
    .out15(WR15), .in(PC_1), .sel(multiplexer_2_out));
  Register #(.width(16)) u_R11 (.D(WR11), .en(Halt), .Q(R11), .clk(CLK), .clr(ResetSig));
  Register #(.width(16)) u_R3 (.D(WR3), .en(Halt), .Q(R3), .clk(CLK), .clr(ResetSig));
  Adder #(.width(16)) adder_2 (.a(PC), .b(16'h1), .out(PC_1));  // open: cin, cout
  Register #(.width(16)) u_R12 (.D(WR12), .en(Halt), .Q(R12), .clk(CLK), .clr(ResetSig));
  Register #(.width(16)) u_R4 (.D(WR4), .en(Halt), .Q(R4), .clk(CLK), .clr(ResetSig));
  Register #(.width(16)) u_R13 (.D(WR13), .en(Halt), .Q(R13), .clk(CLK), .clr(ResetSig));
  Register #(.width(16)) u_R5 (.en(Halt), .Q(R5), .clk(CLK), .clr(ResetSig));  // open: D
  Register #(.width(16)) u_R14 (.D(WR14), .en(Halt), .Q(R14), .clk(CLK), .clr(ResetSig));
  Register #(.width(16)) u_R6 (.D(WR6), .en(Halt), .Q(R6), .clk(CLK), .clr(ResetSig));
  Register #(.width(16)) u_R15 (.D(WR15), .en(Halt), .Q(R15), .clk(CLK), .clr(ResetSig));
  Register #(.width(16)) u_R7 (.D(WR7), .en(Halt), .Q(R7), .clk(CLK), .clr(ResetSig));

  // Other names for the same wires on the sheet: OP[4:0] = opcode

  // Notes on the sheet:
  //   Circuit pour lire dans le registre pointé par SP
  //   Le multiplexeur oriente vers la sortie  du registre pointé (lecture)
  //   si Halt vaut 0 les registres ne répondent plus aux tics d'horloge
  //   Circuit qui agglomere tous les bits des indicateurs calculés dans plusieurs sous-circuits
  //   et donne en sortie les indicateurs SPsel et Wsel sur 2 bits
  //   Le multiplexeur oriente vers la sortie  du registre pointé (lecture)
  //   resteSig remet tous les registres à 0 si à l'état 1
  //   Circuit pour lire dans le registre pointé par SP+1
  //   la pile est constitué de nombreux registres connectés à la meme horloge
  //   incrémente, décrémente, passe à 0 ou laisse à 0 la valeur  du registre SP à chaque instruction en fonction de SPsel
  //   R est la sortie des registres pour lire les données 
  //   WR est l'entrée des registre pour ecrire les données
  //   Circuit pour écrire dans un registre
  //   Même principe, seulement on accès à l’entrée du registre (écriture)
  //   On utilise un multiplexeur annexe car on doit pouvoir
  //   écrire dans SP, SP+1 ou SP-1. Cette information est donnée par Wsel
  //   On passe directement PC+1
  //   car c'est la seule valeur qui peut être ecrite dans la pile d'appel lors d'un call
endmodule

module Indicateurs_Pile_D (
  input  [4:0] opcode,
  output [1:0] SPselData,
  output [1:0] WSselData
);

  SPsel1DATA spsel1data_1 (
    .MSB(opcode[4]), .in_2(opcode[3]), .in_3(opcode[2]), .in_4(opcode[1]), .LSB(opcode[0]),
    .SPsel1data(SPselData[1]));
  SPsel2DATA spsel2data_1 (
    .MSB(opcode[4]), .in_2(opcode[3]), .in_3(opcode[2]), .in_4(opcode[1]), .LSB(opcode[0]),
    .SPsel2data(SPselData[0]));
  WSel1DATA wsel1data_1 (
    .MSB(opcode[4]), .in_2(opcode[3]), .in_3(opcode[2]), .in_4(opcode[1]), .LSB(opcode[0]),
    .Wsel1DATA(WSselData[1]));
  WSel2DATA wsel2data_1 (
    .MSB(opcode[4]), .in_2(opcode[3]), .in_3(opcode[2]), .in_4(opcode[1]), .LSB(opcode[0]),
    .Wsel2DATA(WSselData[0]));

  // Other names for the same wires on the sheet: SPsel2DATA = SPselData[0]; SPsel1DATA = SPselData[1];
  //   WSel2DATA = WSselData[0]; WSel1DATA = WSselData[1]

  // Notes on the sheet:
  //   Circuit qui agglomere tous les bits des indicateurs calculés dans plusieurs sous-circuits
  //   et donne en sortie les indicateurs SPsel et Wsel sur 2 bits
endmodule

module Indicateurs_Pile_A (
  input  [4:0] opcode,
  output [1:0] SPselC,
  output [1:0] WSselC
);

  SPsel1C spsel1c_1 (
    .MSB(opcode[4]), .in_2(opcode[3]), .in_3(opcode[2]), .in_4(opcode[1]), .LSB(opcode[0]),
    .SPsel1C(SPselC[1]));
  SPsel2C spsel2c_1 (
    .MSB(opcode[4]), .in_2(opcode[3]), .in_3(opcode[2]), .in_4(opcode[1]), .LSB(opcode[0]),
    .SPsel2C(SPselC[0]));
  WSel1C wsel1c_1 (
    .MSB(opcode[4]), .in_2(opcode[3]), .in_3(opcode[2]), .in_4(opcode[1]), .LSB(opcode[0]), .WSel1C(WSselC[1]));
  WSel2C wsel2c_1 (
    .MSB(opcode[4]), .in_2(opcode[3]), .in_3(opcode[2]), .in_4(opcode[1]), .LSB(opcode[0]), .WSel2C(WSselC[0]));

  // Other names for the same wires on the sheet: SPsel2C = SPselC[0]; SPsel1C = SPselC[1]; WSel2C = WSselC[0];
  //   WSel1C = WSselC[1]

  // Notes on the sheet:
  //   Circuit qui agglomere tous les bits des indicateurs calculés dans plusieurs sous-circuits
  //   et donne en sortie les indicateurs SPsel et Wsel sur 2 bits (pour la pile d'appel)
endmodule

module Update_PC (
  input  [5:0] opcode,
  input  [15:0] Stack_SP,
  input  [15:0] instr_parameter,
  input  [15:0] ResultatTest,
  input  [15:0] PreviousPC,
  output [15:0] New_PC
);

  wire ResultatTest_t;
  wire [15:0] jmpf, jmpt, PC_1;

  Multiplexer #(.select(5), .width(16), .enable("false")) multiplexer_1 (
    .in0(PC_1), .in1(PC_1), .in2(PC_1), .in3(PC_1), .in4(PC_1), .in5(PC_1), .in6(PC_1), .in7(PC_1),
    .in8(PC_1), .in9(PC_1), .in10(PC_1), .in11(PC_1), .in12(PC_1), .in13(PC_1), .in14(instr_parameter),
    .in15(jmpt), .in16(jmpf), .in17(PC_1), .in18(PC_1), .in19(PC_1), .in20(PC_1), .in21(instr_parameter),
    .in22(Stack_SP), .in23(PC_1), .in24(PC_1), .in25(PC_1), .in26(PC_1), .in27(PC_1), .in28(PC_1),
    .in29(PC_1), .in30(PC_1), .in31(PC_1), .out(New_PC), .sel(opcode[4:0]));
  Adder #(.width(16)) adder_1 (.a(PreviousPC), .b(16'h1), .out(PC_1));  // open: cin, cout
  Multiplexer #(.width(16), .enable("false")) multiplexer_2 (
    .in0(instr_parameter), .in1(PC_1), .out(jmpf), .sel(ResultatTest_t));
  BitSelector #(.width(16)) bitselector_1 (.in(ResultatTest), .out(ResultatTest_t), .sel(4'b0000));
  Multiplexer #(.width(16), .enable("false")) multiplexer_3 (
    .in0(PC_1), .in1(instr_parameter), .out(jmpt), .sel(ResultatTest_t));

  // Other names for the same wires on the sheet: Parameter[15:0] = instr_parameter

  // Notes on the sheet:
  //   Il y a 3 cas :
  //   soit PC prend la valeur PC+1
  //   soit il prend une valeur passée en pararmetre lors d'un jump
  //   soit il prend la valeur du haut de la pile d'appel
  //   On utilise un multiplexeur avec un selecteur qui est l'opcode
  //   Il y a 2 cas pour le jmpf et le jmpt :
  //   PC devient PC+1 ou le parametre en fonction du résultat du test
  //   Il y a 2 cas pour le jmpf et le jmpt :
  //   PC devient PC+1 ou le parametre en fonction du résultat du test
endmodule

module Controlleur (
  input  [5:0] OPCODE,
  input  resetSig,
  output Halt,
  output isPushAdr,
  output isPopAdr,
  output [5:0] _6_OP,
  output [4:0] _5_OP,
  output [3:0] _4_OP,
  output ResetSig_2,
  output [1:0] SpselD,
  output [1:0] WselD,
  output [1:0] SPselC,
  output [1:0] WselC,
  output [2:0] WhereToWrite
);

  Multiplexer #(.select(5), .width(3), .enable("false")) multiplexer_1 (
    .in0(3'b000), .in1(3'b000), .in2(3'b000), .in3(3'b000), .in4(3'b000), .in5(3'b000), .in6(3'b000),
    .in7(3'b000), .in8(3'b000), .in9(3'b000), .in10(3'b000), .in11(3'b001), .in12(3'b001), .in13(3'b001),
    .in14(3'b010), .in15(3'b010), .in16(3'b010), .in17(3'b011), .in18(3'b100), .in19(3'b011), .in20(3'b010),
    .in21(3'b010), .in22(3'b010), .in23(3'b010), .in24(3'b010), .in25(3'b010), .in26(3'b010), .in27(3'b010),
    .in28(3'b010), .in29(3'b010), .in30(3'b010), .in31(3'b010), .out(WhereToWrite), .sel(OPCODE[4:0]));
  and and_1 (isPushAdr, ~OPCODE[5], OPCODE[4], ~OPCODE[3], ~OPCODE[2], OPCODE[1], ~OPCODE[0]);  // AND_Gate
  and and_2 (isPopAdr, ~OPCODE[5], OPCODE[4], ~OPCODE[3], OPCODE[2], ~OPCODE[1], ~OPCODE[0]);  // AND_Gate
  Indicateurs_Pile_D Data (.opcode(OPCODE[4:0]), .SPselData(SpselD), .WSselData(WselD));
  Indicateurs_Pile_A Call (.opcode(OPCODE[4:0]), .SPselC(SPselC), .WSselC(WselC));
  nand nand_1 (Halt, OPCODE[3], OPCODE[4]);

  assign _4_OP = OPCODE[3:0];
  assign _5_OP = OPCODE[4:0];
  assign _6_OP = OPCODE;
  assign ResetSig_2 = resetSig;

  // Other names for the same wires on the sheet: _4_OPCODE[3:0] = OPCODE[3:0]; _5_OPCODE[4:0] = OPCODE[4:0];
  //   _6_OPCODE[5:0] = OPCODE

  // Notes on the sheet:
  //   on décline l'opcode sur 4, 5 et 6 bits
  //   signal qui test si l'instructution courante est un pop adr
  //   signal qui test si l'instructution courante est un push adr
  //   fonctionne en regroupant les instructions en groupe
  //   qui oriente la même entrée dans stack sp
  //   fonctionnement détaillé expliqué dans le rapport en partie 5
  //   genere le sélécteur du multiplexeur dans le fifth qui oriente la bonne entrée dans stack sp
  //   signal qui test si l'instructution courante est un halt
endmodule

module Flags (
  input  [15:0] RESULT,
  input  [15:0] A,
  input  [15:0] B,
  input  [3:0] OPCODE,
  output [2:0] Flags
);

  wire Sign_bit_A, Sign_bit_B, Sign_bit_Sortie;

  BitSelector #(.width(16)) bitselector_1 (.in(A), .out(Sign_bit_A), .sel(4'b0000));
  BitSelector #(.width(16)) bitselector_2 (.in(B), .out(Sign_bit_B), .sel(4'b0000));
  BitSelector #(.width(16)) bitselector_3 (.in(RESULT), .out(Sign_bit_Sortie), .sel(4'b0000));
  nor nor_1 (Flags[0], RESULT[0], RESULT[1], RESULT[2], RESULT[3], RESULT[4], RESULT[5], RESULT[6], RESULT[7], RESULT[9], RESULT[10], RESULT[11], RESULT[12], RESULT[13], RESULT[14], RESULT[15], RESULT[8]);
  Overflow_Flag overflow_flag_1 (
    .Signe_A(Sign_bit_A), .Signe_B(Sign_bit_B), .Signe_Sortie(Sign_bit_Sortie), .opCode(OPCODE), .OF(Flags[2]));

  assign Flags[1] = RESULT[15];

  // Other names for the same wires on the sheet: ZeroFlag = Flags[0]; SignFlag = RESULT[15]; OF = Flags[2]

  // Notes on the sheet:
  //   récupere le bit de signe de A et B
  //   pour tester si un nombre est 0 on effectue un XOR de tous ses bits
  //   Calcule l'overflow flag
endmodule

module Overflow_Flag (
  input  Signe_A,
  input  Signe_B,
  input  Signe_Sortie,
  input  [3:0] opCode,
  output OF
);

  wire add, and_1_out, and_2_out, and_3_out, and_4_out, sub;

  and and_1 (and_1_out, ~Signe_A, ~Signe_B, Signe_Sortie);  // AND_Gate
  and and_2 (and_2_out, Signe_A, Signe_B, ~Signe_Sortie);  // AND_Gate
  and and_3 (and_3_out, ~Signe_A, Signe_B, Signe_Sortie);  // AND_Gate
  and and_4 (and_4_out, Signe_A, ~Signe_B, ~Signe_Sortie);  // AND_Gate
  or or_1 (add, and_1_out, and_2_out);
  or or_2 (sub, and_3_out, and_4_out);
  Multiplexer #(.select(4), .enable("false")) multiplexer_1 (
    .in0(add), .in1(sub), .in12(sub), .in13(sub), .in14(sub), .out(OF), .sel(opCode));  // open: in2, in3, in4, in5, in6, in7, in8, in9, in10, in11, in15

  // Notes on the sheet:
  //   implémentation en circuit de la table de vérité donnée dans le rapport pour calculer l'OF
  //   L'OF est levé lors d'une soustraction et d'une addition (opcode 0000 et 0001) 
  //   Nous vons aussi besoin de calculer l'OF quand on réalise un test (on récupere les flag comme si on avait effectuer une soustraction) 
  //   on ne calcule OF que pour les instructions qui nous intéressent
  //   on aurait pu le faire pour tous mais ça n'aurait pas été utile car il n'aurait pas été utilisé
endmodule

module SPsel1DATA (
  input  MSB,
  input  in_2,
  input  in_3,
  input  in_4,
  input  LSB,
  output SPsel1data
);

  wire and_1_out, and_2_out, and_3_out, and_4_out, and_5_out;

  and and_1 (and_1_out, MSB, in_2);
  and and_2 (and_2_out, ~in_2, in_4, ~LSB);  // AND_Gate
  and and_3 (and_3_out, in_3, in_4, ~LSB);  // AND_Gate
  and and_4 (and_4_out, MSB, ~in_4, LSB);  // AND_Gate
  and and_5 (and_5_out, MSB, in_3, LSB);
  or or_1 (SPsel1data, and_1_out, and_2_out, and_3_out, and_4_out, and_5_out);

  // Notes on the sheet:
  //   tous les circuits à suivre calculent chacun 1 bit des indicateurs SPsel et Wsel
  //   poiur chacune des piles
  //   réalisation des circuits justifiée dans l'annexe du rapport 
endmodule

module SPsel2DATA (
  input  MSB,
  input  in_2,
  input  in_3,
  input  in_4,
  input  LSB,
  output SPsel2data
);

  wire and_1_out, and_2_out, and_3_out, and_4_out, and_5_out;

  and and_1 (and_1_out, ~MSB, ~in_4);  // AND_Gate
  and and_2 (and_2_out, in_4, LSB);
  and and_3 (and_3_out, ~in_2, ~in_4, ~LSB);  // AND_Gate
  and and_4 (and_4_out, ~MSB, in_2, ~in_3);  // AND_Gate
  and and_5 (and_5_out, MSB, ~in_2, ~in_3);  // AND_Gate
  or or_1 (SPsel2data, and_1_out, and_2_out, and_3_out, and_4_out, and_5_out);
endmodule

module SPsel1C (
  input  MSB,
  input  in_2,
  input  in_3,
  input  in_4,
  input  LSB,
  output SPsel1C
);

  or or_1 (SPsel1C, ~MSB, ~in_3, ~in_4, LSB);  // OR_Gate
endmodule

module SPsel2C (
  input  MSB,
  input  in_2,
  input  in_3,
  input  in_4,
  input  LSB,
  output SPsel2C
);

  wire and_1_out, and_2_out;

  and and_1 (and_1_out, MSB, in_3, ~in_4, LSB);  // AND_Gate
  and and_2 (and_2_out, MSB, in_3, in_4, ~LSB);  // AND_Gate
  or or_1 (SPsel2C, and_1_out, and_2_out);
endmodule

module WSel1DATA (
  input  MSB,
  input  in_2,
  input  in_3,
  input  in_4,
  input  LSB,
  output Wsel1DATA
);

  wire and_1_out, and_2_out, and_3_out, and_4_out, and_5_out, and_6_out;

  and and_1 (and_1_out, ~MSB, LSB);  // AND_Gate
  and and_2 (and_2_out, ~MSB, in_2);  // AND_Gate
  and and_3 (and_3_out, ~in_3, ~in_4, ~LSB);  // AND_Gate
  and and_4 (and_4_out, ~in_2, in_3, ~in_4);  // AND_Gate
  and and_5 (and_5_out, ~in_2, ~in_3, in_4, LSB);  // AND_Gate
  and and_6 (and_6_out, MSB, ~in_2, in_3, ~LSB);  // AND_Gate
  or or_1 (Wsel1DATA, and_1_out, and_2_out, and_3_out, and_4_out, and_5_out, and_6_out);
endmodule

module WSel2DATA (
  input  MSB,
  input  in_2,
  input  in_3,
  input  in_4,
  input  LSB,
  output Wsel2DATA
);

  wire and_1_out;

  and and_1 (and_1_out, in_2, in_3, in_4);
  or or_1 (Wsel2DATA, MSB, and_1_out);
endmodule

module WSel1C (
  input  MSB,
  input  in_2,
  input  in_3,
  input  in_4,
  input  LSB,
  output WSel1C
);

  or or_1 (WSel1C, ~MSB, ~in_3, ~LSB, in_4);  // OR_Gate
endmodule

module WSel2C (
  input  MSB,
  input  in_2,
  input  in_3,
  input  in_4,
  input  LSB,
  output WSel2C
);


  assign WSel2C = 1'b1;
endmodule
